// Logisim project von-neumann.circ as structural Verilog: 7 circuits, main circuit 4bit adder
module _4bit_adder (
  input  in_1,
  input  in_2,
  input  in_3,
  input  in_4,
  input  in_5,
  input  in_6,
  input  in_7,
  input  in_8,
  input  subtract,
  output out_10,
  output out_11,
  output out_12,
  output out_13,
  output out_14
);

  wire and_1_out, and_2_out, and_3_out, and_4_out, and_5_out, and_6_out, and_7_out, and_8_out, or_1_out,
       or_2_out, or_3_out, xor_1_out, xor_2_out, xor_3_out, xor_4_out, xor_5_out, xor_6_out, xor_7_out,
       xor_8_out;

  xor xor_1 (xor_1_out, in_5, subtract);
  xor xor_2 (xor_2_out, in_6, subtract);
  xor xor_3 (xor_3_out, in_7, subtract);
  xor xor_4 (xor_4_out, in_8, subtract);
  and and_1 (and_1_out, or_1_out, xor_1_out);
  xor xor_5 (xor_5_out, or_1_out, xor_1_out);
  and and_2 (and_2_out, or_2_out, xor_2_out);
  xor xor_6 (xor_6_out, or_2_out, xor_2_out);
  and and_3 (and_3_out, or_3_out, xor_3_out);
  xor xor_7 (xor_7_out, or_3_out, xor_3_out);
  and and_4 (and_4_out, subtract, xor_4_out);
  xor xor_8 (xor_8_out, subtract, xor_4_out);
  and and_5 (and_5_out, xor_5_out, in_1);
  xor xor_9 (out_11, xor_5_out, in_1);
  and and_6 (and_6_out, xor_6_out, in_2);
  xor xor_10 (out_12, xor_6_out, in_2);
  and and_7 (and_7_out, xor_7_out, in_3);
  xor xor_11 (out_13, xor_7_out, in_3);
  and and_8 (and_8_out, xor_8_out, in_4);
  xor xor_12 (out_14, xor_8_out, in_4);
  or or_1 (or_1_out, and_6_out, and_2_out);
  or or_2 (or_2_out, and_7_out, and_3_out);
  or or_3 (or_3_out, and_8_out, and_4_out);
  or or_4 (out_10, and_5_out, and_1_out);
endmodule

module von_neumann (
  input  writing_mode,
  input  [8:0] in_2,
  input  [7:0] in_3,
  input  clear,
  input  programming_mode,
  input  update,
  input  [7:0] in_7,
  input  in_8,
  input  [7:0] in_9,
  input  in_10,
  output [8:0] out_11,
  output [3:0] out_12,
  output [3:0] out_13,
  output [3:0] out_14,
  output [3:0] out_15
);

  wire add, adder_out_10, and_1_out, clk, cmp, comparator_1_eq, controlled_buffer_1_out,
       controlled_buffer_11_out, controlled_buffer_13_out, controlled_buffer_17_out, ld, not_1_out,
       not_2_out, not_3_out, not_4_out, not_5_out, not_6_out, not_7_out, not_8_out, not_9_out, not_10_out,
       not_11_out, not_12_out, not_13_out, not_14_out, not_15_out, not_16_out, not_17_out, not_18_out,
       not_19_out, not_20_out, or_1_out, or_2_out, or_3_out, or_4_out, psh, st, sub, v_a;
  wire [2:0] comperator_out_11;
  wire [3:0] adder_out_14, addr, controlled_buffer_2_out, controlled_buffer_3_out, controlled_buffer_4_out,
       controlled_buffer_5_out, controlled_buffer_15_out, ram_2_data, register_1_q, result;
  wire [7:0] controlled_buffer_6_out, operation_counter_out_6;
  wire [8:0] controlled_buffer_12_out;

  assign controlled_buffer_1_out = not_4_out ? clk : 1'bz;  // Controlled_Buffer controlled_buffer_1
  assign controlled_buffer_2_out = or_1_out ? out_14 : 4'bz;  // Controlled_Buffer controlled_buffer_2
  assign controlled_buffer_3_out = cmp ? out_14 : 4'bz;  // Controlled_Buffer controlled_buffer_3
  operation_counter operation_counter (
    .clock(controlled_buffer_1_out), .val(in_7), .subtract(in_8), .out_6(operation_counter_out_6),
    .jump_to(in_9), .jump_mode(in_10));
  or or_1 (or_1_out, add, sub);
  assign controlled_buffer_4_out = or_1_out ? out_12 : 4'bz;  // Controlled_Buffer controlled_buffer_4
  assign controlled_buffer_5_out = cmp ? out_12 : 4'bz;  // Controlled_Buffer controlled_buffer_5
  assign controlled_buffer_6_out = programming_mode ? in_3 : 8'bz;  // Controlled_Buffer controlled_buffer_6
  not not_1 (not_1_out, programming_mode);
  assign controlled_buffer_6_out = not_1_out ? operation_counter_out_6 : 8'bz;  // Controlled_Buffer controlled_buffer_7
  not not_2 (not_2_out, comparator_1_eq);
  Comparator #(.width(4)) comparator_1 (.a(out_12), .b(result), .eq(comparator_1_eq));  // open: gt, lt
  assign out_11 = writing_mode ? in_2 : 9'bz;  // Controlled_Buffer controlled_buffer_8
  not not_3 (not_3_out, writing_mode);
  not not_4 (not_4_out, and_1_out);
  and and_1 (and_1_out, psh, not_2_out);
  LED led_1 (.in(adder_out_10));
  _4bit_adder adder (
    .in_1(controlled_buffer_4_out[3]), .in_2(controlled_buffer_4_out[2]), .in_3(controlled_buffer_4_out[1]),
    .in_4(controlled_buffer_4_out[0]), .in_5(controlled_buffer_2_out[3]), .in_6(controlled_buffer_2_out[2]),
    .in_7(controlled_buffer_2_out[1]), .in_8(controlled_buffer_2_out[0]), .subtract(sub),
    .out_10(adder_out_10), .out_11(adder_out_14[3]), .out_12(adder_out_14[2]), .out_13(adder_out_14[1]),
    .out_14(adder_out_14[0]));
  assign out_15 = or_1_out ? adder_out_14 : 4'bz;  // Controlled_Buffer controlled_buffer_9
  assign out_15 = cmp ? {1'b0, comperator_out_11} : 4'bz;  // Controlled_Buffer controlled_buffer_10
  _4bit_comperator comperator (
    .in_1(controlled_buffer_5_out[3]), .in_2(controlled_buffer_5_out[2]), .in_3(controlled_buffer_5_out[1]),
    .in_4(controlled_buffer_5_out[0]), .in_5(controlled_buffer_3_out[0]), .in_6(controlled_buffer_3_out[1]),
    .in_7(controlled_buffer_3_out[2]), .in_8(controlled_buffer_3_out[3]), .out_9(comperator_out_11[2]),
    .out_10(comperator_out_11[1]), .out_11(comperator_out_11[0]));
  _4bit_register u_result (
    .in_1(clk), .in_2(out_15[3]), .in_3(out_15[2]), .in_4(out_15[1]), .in_5(out_15[0]), .out_6(result[3]),
    .out_7(result[2]), .out_8(result[1]), .out_9(result[0]));
  RAM #(.dataWidth(9)) ram_1 (
    .addr(controlled_buffer_6_out), .data(out_11), .clk(update), .ld(not_3_out), .clr(clear));  // open: sel
  assign controlled_buffer_11_out = not_4_out ? clk : 1'bz;  // Controlled_Buffer controlled_buffer_11
  assign controlled_buffer_12_out = not_1_out ? out_11 : 9'bz;  // Controlled_Buffer controlled_buffer_12
  Register #(.width(9)) register_1 (
    .D(controlled_buffer_12_out), .Q({addr[0], addr[1], addr[2], addr[3], v_a, register_1_q}),
    .clk(controlled_buffer_11_out));  // open: en, clr
  Clock #(.highDuration(10), .lowDuration(10)) clock_1 (.out(clk));
  not not_5 (not_5_out, register_1_q[0]);
  not not_6 (not_6_out, register_1_q[1]);
  not not_7 (not_7_out, register_1_q[2]);
  not not_8 (not_8_out, register_1_q[3]);
  not not_9 (not_9_out, register_1_q[0]);
  not not_10 (not_10_out, register_1_q[1]);
  not not_11 (not_11_out, register_1_q[2]);
  not not_12 (not_12_out, register_1_q[0]);
  not not_13 (not_13_out, register_1_q[2]);
  not not_14 (not_14_out, register_1_q[3]);
  not not_15 (not_15_out, register_1_q[0]);
  not not_16 (not_16_out, register_1_q[2]);
  not not_17 (not_17_out, register_1_q[0]);
  not not_18 (not_18_out, register_1_q[3]);
  not not_19 (not_19_out, register_1_q[0]);
  and and_2 (ld, not_5_out, not_6_out, not_7_out, not_8_out);
  and and_3 (st, not_9_out, not_10_out, not_11_out, register_1_q[3]);
  and and_4 (add, not_12_out, register_1_q[1], not_13_out, not_14_out);
  and and_5 (sub, not_15_out, register_1_q[1], not_16_out, register_1_q[3]);
  and and_6 (cmp, not_17_out, register_1_q[1], register_1_q[2], not_18_out);
  and and_7 (psh, not_19_out, register_1_q[1], register_1_q[2], register_1_q[3]);
  or or_2 (or_2_out, ld, or_3_out);
  assign controlled_buffer_13_out = st ? clk : 1'bz;  // Controlled_Buffer controlled_buffer_13
  RAM #(.addrWidth(4), .dataWidth(4)) ram_2 (
    .addr(addr), .data(ram_2_data), .clk(controlled_buffer_13_out), .ld(or_2_out));  // open: sel, clr
  assign ram_2_data = st ? out_12 : 4'bz;  // Controlled_Buffer controlled_buffer_14
  or or_3 (or_3_out, add, sub, cmp);
  assign controlled_buffer_15_out = v_a ? addr : 4'bz;  // Controlled_Buffer controlled_buffer_15
  not not_20 (not_20_out, v_a);
  assign controlled_buffer_15_out = not_20_out ? ram_2_data : 4'bz;  // Controlled_Buffer controlled_buffer_16
  assign controlled_buffer_17_out = or_4_out ? clk : 1'bz;  // Controlled_Buffer controlled_buffer_17
  assign controlled_buffer_15_out = psh ? result : 4'bz;  // Controlled_Buffer controlled_buffer_18
  or or_4 (or_4_out, ld, psh);
  _4bit_register akku (
    .in_1(controlled_buffer_17_out), .in_2(controlled_buffer_15_out[3]), .in_3(controlled_buffer_15_out[2]),
    .in_4(controlled_buffer_15_out[1]), .in_5(controlled_buffer_15_out[0]), .out_6(out_12[3]),
    .out_7(out_12[2]), .out_8(out_12[1]), .out_9(out_12[0]));
  assign out_14 = or_3_out ? controlled_buffer_15_out : 4'bz;  // Controlled_Buffer controlled_buffer_19

  assign out_13 = out_12;

  // Other names for the same wires on the sheet: val[3:0] = addr; akku[3:0] = out_12; operand[3:0] = out_14
endmodule

module _4bit_comperator (
  input  in_1,
  input  in_2,
  input  in_3,
  input  in_4,
  input  in_5,
  input  in_6,
  input  in_7,
  input  in_8,
  output out_9,
  output out_10,
  output out_11
);

  Comparator #(.width(4)) comparator_1 (
    .a({in_1, in_2, in_3, in_4}), .b({in_5, in_6, in_7, in_8}), .gt(out_9), .eq(out_10), .lt(out_11));
endmodule

module _4bit_register (
  input  in_1,
  input  in_2,
  input  in_3,
  input  in_4,
  input  in_5,
  output out_6,
  output out_7,
  output out_8,
  output out_9
);

  D_Flip_Flop d_ff_1 (.clk(in_1), .D(in_2), .Q(out_6));  // open: Qn, preset, en, reset
  D_Flip_Flop d_ff_2 (.clk(in_1), .D(in_3), .Q(out_7));  // open: Qn, preset, en, reset
  D_Flip_Flop d_ff_3 (.clk(in_1), .D(in_4), .Q(out_8));  // open: Qn, preset, en, reset
  D_Flip_Flop d_ff_4 (.clk(in_1), .D(in_5), .Q(out_9));  // open: Qn, preset, en, reset
endmodule

module _8bit_register (
  input  in_1,
  input  in_2,
  input  in_3,
  input  in_4,
  input  in_5,
  input  in_6,
  input  in_7,
  input  in_8,
  input  in_9,
  output out_10,
  output out_11,
  output out_12,
  output out_13,
  output out_14,
  output out_15,
  output out_16,
  output out_17
);

  D_Flip_Flop d_ff_1 (.clk(in_1), .D(in_2), .Q(out_10));  // open: Qn, preset, en, reset
  D_Flip_Flop d_ff_2 (.clk(in_1), .D(in_3), .Q(out_11));  // open: Qn, preset, en, reset
  D_Flip_Flop d_ff_3 (.clk(in_1), .D(in_4), .Q(out_12));  // open: Qn, preset, en, reset
  D_Flip_Flop d_ff_4 (.clk(in_1), .D(in_5), .Q(out_13));  // open: Qn, preset, en, reset
  D_Flip_Flop d_ff_5 (.clk(in_1), .D(in_6), .Q(out_14));  // open: Qn, preset, en, reset
  D_Flip_Flop d_ff_6 (.clk(in_1), .D(in_7), .Q(out_15));  // open: Qn, preset, en, reset
  D_Flip_Flop d_ff_7 (.clk(in_1), .D(in_8), .Q(out_16));  // open: Qn, preset, en, reset
  D_Flip_Flop d_ff_8 (.clk(in_1), .D(in_9), .Q(out_17));  // open: Qn, preset, en, reset
endmodule

module _8bit_adder (
  input  in_1,
  input  in_2,
  input  in_3,
  input  in_4,
  input  in_5,
  input  in_6,
  input  in_7,
  input  in_8,
  input  in_9,
  input  in_10,
  input  in_11,
  input  in_12,
  input  in_13,
  input  in_14,
  input  in_15,
  input  in_16,
  input  subtract,
  output out_18,
  output out_19,
  output out_20,
  output out_21,
  output out_22,
  output out_23,
  output out_24,
  output out_25,
  output out_26
);

  wire and_1_out, and_2_out, and_3_out, and_4_out, and_5_out, and_6_out, and_7_out, and_8_out, and_9_out,
       and_10_out, and_11_out, and_12_out, and_13_out, and_14_out, and_15_out, and_16_out, or_2_out,
       or_3_out, or_4_out, or_5_out, or_6_out, or_7_out, or_8_out, xor_1_out, xor_2_out, xor_3_out,
       xor_4_out, xor_5_out, xor_6_out, xor_7_out, xor_8_out, xor_9_out, xor_10_out, xor_11_out, xor_12_out,
       xor_13_out, xor_14_out, xor_15_out, xor_16_out;

  xor xor_1 (xor_1_out, in_9, subtract);
  xor xor_2 (xor_2_out, in_10, subtract);
  xor xor_3 (xor_3_out, in_11, subtract);
  xor xor_4 (xor_4_out, in_12, subtract);
  xor xor_5 (xor_5_out, in_13, subtract);
  xor xor_6 (xor_6_out, in_14, subtract);
  xor xor_7 (xor_7_out, in_15, subtract);
  xor xor_8 (xor_8_out, in_16, subtract);
  and and_1 (and_1_out, or_3_out, in_2);
  and and_2 (and_2_out, or_4_out, xor_3_out);
  and and_3 (and_3_out, or_7_out, xor_6_out);
  and and_4 (and_4_out, or_8_out, xor_7_out);
  and and_5 (and_5_out, or_2_out, xor_1_out);
  xor xor_9 (xor_9_out, or_2_out, xor_1_out);
  xor xor_10 (xor_10_out, or_3_out, in_2);
  xor xor_11 (xor_11_out, or_4_out, xor_3_out);
  and and_6 (and_6_out, or_5_out, xor_4_out);
  xor xor_12 (xor_12_out, or_5_out, xor_4_out);
  and and_7 (and_7_out, or_6_out, xor_5_out);
  xor xor_13 (xor_13_out, or_6_out, xor_5_out);
  xor xor_14 (xor_14_out, or_7_out, xor_6_out);
  xor xor_15 (xor_15_out, or_8_out, xor_7_out);
  and and_8 (and_8_out, subtract, xor_8_out);
  xor xor_16 (xor_16_out, subtract, xor_8_out);
  and and_9 (and_9_out, xor_9_out, in_1);
  xor xor_17 (out_19, xor_9_out, in_1);
  and and_10 (and_10_out, xor_10_out, xor_2_out);
  xor xor_18 (out_20, xor_10_out, xor_2_out);
  and and_11 (and_11_out, xor_11_out, in_3);
  xor xor_19 (out_21, xor_11_out, in_3);
  and and_12 (and_12_out, xor_12_out, in_4);
  xor xor_20 (out_22, xor_12_out, in_4);
  and and_13 (and_13_out, xor_13_out, in_5);
  xor xor_21 (out_23, xor_13_out, in_5);
  and and_14 (and_14_out, xor_14_out, in_6);
  xor xor_22 (out_24, xor_14_out, in_6);
  and and_15 (and_15_out, xor_15_out, in_7);
  xor xor_23 (out_25, xor_15_out, in_7);
  and and_16 (and_16_out, xor_16_out, in_8);
  xor xor_24 (out_26, xor_16_out, in_8);
  or or_1 (out_18, and_9_out, and_5_out);
  or or_2 (or_2_out, and_10_out, and_1_out);
  or or_3 (or_3_out, and_11_out, and_2_out);
  or or_4 (or_4_out, and_12_out, and_6_out);
  or or_5 (or_5_out, and_13_out, and_7_out);
  or or_6 (or_6_out, and_14_out, and_3_out);
  or or_7 (or_7_out, and_15_out, and_4_out);
  or or_8 (or_8_out, and_16_out, and_8_out);
endmodule

module operation_counter (
  input  clock,
  input  [7:0] val,
  input  subtract,
  input  [7:0] jump_to,
  input  jump_mode,
  output [7:0] out_6
);

  wire n8bit_adder_1_out_19, n8bit_adder_1_out_20, n8bit_adder_1_out_21, n8bit_adder_1_out_22,
       n8bit_adder_1_out_23, n8bit_adder_1_out_24, n8bit_adder_1_out_25, n8bit_adder_1_out_26, not_1_out;
  wire [7:0] controlled_buffer_1_out;

  _8bit_adder u_8bit_adder_1 (
    .out_19(n8bit_adder_1_out_19), .out_20(n8bit_adder_1_out_20), .in_1(controlled_buffer_1_out[7]),
    .out_21(n8bit_adder_1_out_21), .in_2(controlled_buffer_1_out[6]), .in_3(controlled_buffer_1_out[5]),
    .in_4(controlled_buffer_1_out[4]), .out_22(n8bit_adder_1_out_22), .in_5(controlled_buffer_1_out[3]),
    .in_6(controlled_buffer_1_out[2]), .in_7(controlled_buffer_1_out[1]), .in_8(controlled_buffer_1_out[0]),
    .in_9(val[7]), .in_10(val[6]), .in_11(val[5]), .in_12(val[4]), .in_13(val[3]), .in_14(val[2]),
    .in_15(val[1]), .in_16(val[0]), .subtract(subtract), .out_23(n8bit_adder_1_out_23),
    .out_24(n8bit_adder_1_out_24), .out_25(n8bit_adder_1_out_25), .out_26(n8bit_adder_1_out_26));  // open: out_18
  assign controlled_buffer_1_out = jump_mode ? jump_to : 8'bz;  // Controlled_Buffer controlled_buffer_1
  _8bit_register u_8bit_register_1 (
    .in_1(clock), .in_2(n8bit_adder_1_out_19), .in_3(n8bit_adder_1_out_20), .in_4(n8bit_adder_1_out_21),
    .in_5(n8bit_adder_1_out_22), .in_6(n8bit_adder_1_out_23), .in_7(n8bit_adder_1_out_24),
    .in_8(n8bit_adder_1_out_25), .in_9(n8bit_adder_1_out_26), .out_10(out_6[7]), .out_11(out_6[6]),
    .out_12(out_6[5]), .out_13(out_6[4]), .out_14(out_6[3]), .out_15(out_6[2]), .out_16(out_6[1]),
    .out_17(out_6[0]));
  assign controlled_buffer_1_out = not_1_out ? out_6 : 8'bz;  // Controlled_Buffer controlled_buffer_2
  not not_1 (not_1_out, jump_mode);
endmodule
